# Fritzing sketch AlarmController (saved by Fritzing 0.9.3b)
breadboards: 1

parts:
  U2 = NodeMCU V1.0
  Bus_3v5v1 = TXB0104 4-channel Bi-Directional Level Shifter
  RFID1 = RFID Reader
  HLK-PM1 = HLK-PM01
  S2 = SWITCH-MOMENTARY-2 [package=tactile-switch-1101ne]

nets:
  N1: U2.D2, Bus_3v5v1.A3
  N2: U2.D3, Bus_3v5v1.A4
  N3: U2.3V3, Bus_3v5v1.LV
  GND: U2.GND, Bus_3v5v1.GND, RFID1.CP, HLK-PM1.-Vo
  N4: U2.D5, Bus_3v5v1.A1
  N5: U2.D6, Bus_3v5v1.A2
  N6: U2.Vin, Bus_3v5v1.HV, RFID1.ANT1, HLK-PM1.+Vo
  N7: Bus_3v5v1.B1, RFID1.+5V
  N8: Bus_3v5v1.B2, RFID1.GND
  N9: Bus_3v5v1.B3, RFID1.RES
  N10: Bus_3v5v1.B4, RFID1.ANT0
  N11: HLK-PM1.AC#1, S2.2

custom parts:
  NodeMCU V1.0: ESP8266 based NodeMCU
  TXB0104 4-channel Bi-Directional Level Shifter: Because the Arduino (and Basic Stamp) are 5V devices, and most modern sensors, displays, flash cards and modes are 3.3V-only, many makers find that they need to perform level shifting/conversion to protect the 3.3V device from 5V. Although one can use resistors to make a divider, for high speed transfers, the resistors can add a lot of slew and cause havoc that is tough to debug. For that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
